// Logisim project dflipflop1.circ as structural Verilog
module main (
  input  clk,
  input  d,
  output q,
  output qn
);

  dff dff_1 (.clk(clk), .d(d), .q(q), .qn(qn));
endmodule

// VHDL entity dff, as the project stores it:
library ieee;
use ieee.std_logic_1164.all;

entity dff is
    port (
        clk : in  std_logic;
        d   : in  std_logic;
        q   : out std_logic;
        qn  : out std_logic
    );
end entity dff;

architecture behavioral of dff is
    signal q_i : std_logic := '0';
begin
    process (clk)
    begin
        if rising_edge(clk) then
            q_i <= d;
        end if;
    end process;

    q  <= q_i;
    qn <= not q_i;
end architecture behavioral;
