// Logisim project dflipflop2.circ as structural Verilog: 1 circuit, main circuit main
module main (
  input  D1,
  input  CLK1,
  output Q1,
  output QN1
);

  wire nand_1_out, nand_2_out, nand_3_out, nand_4_out, nand_5_out, nand_6_out, not_1_out, not_2_out,
       not_3_out, not_4_out;

  not not_1 (not_1_out, CLK1);
  not not_2 (not_2_out, D1);
  nand nand_1 (nand_1_out, D1, not_1_out);
  nand nand_2 (nand_2_out, not_1_out, not_2_out);
  nand nand_3 (nand_3_out, nand_1_out, nand_4_out);
  nand nand_4 (nand_4_out, nand_3_out, nand_2_out);
  not not_3 (not_3_out, not_1_out);
  not not_4 (not_4_out, nand_3_out);
  nand nand_5 (nand_5_out, nand_3_out, not_3_out);
  nand nand_6 (nand_6_out, not_3_out, not_4_out);
  nand nand_7 (Q1, nand_5_out, QN1);
  nand nand_8 (QN1, Q1, nand_6_out);

  // Notes on the sheet:
  //   D flip-flop
endmodule
