// Logisim project dlatch2.circ as structural Verilog: 1 circuit, main circuit main
module main (
  input  D1,
  input  en1,
  output Q1,
  output QN1
);

  wire nand_1_out, nand_2_out, not_1_out;

  not not_1 (not_1_out, D1);
  nand nand_1 (nand_1_out, D1, en1);
  nand nand_2 (nand_2_out, en1, not_1_out);
  nand nand_3 (Q1, nand_1_out, QN1);
  nand nand_4 (QN1, Q1, nand_2_out);

  // Notes on the sheet:
  //   D Latch
endmodule
