// Logisim project fjdakl.circ as structural Verilog
module main (
  input  in_1,
  input  in_2,
  input  in_3,
  input  in_4,
  output out_5
);

  dflipflop dflipflop_1 (.clk(in_1), .d(in_2), .clr(in_3), .set(in_4), .q(out_5));
endmodule

// VHDL entity dflipflop, as the project stores it:
library ieee;
use ieee.std_logic_1164.all;
use ieee.numeric_std.all;

entity dflipflop is
    port (
        clk : in  std_logic;  -- Clock signal
        d   : in  std_logic;  -- Data input
        clr : in  std_logic;  -- Asynchronous clear signal
        set : in  std_logic;  -- Asynchronous set signal
        q   : out std_logic   -- Data output
    );
end dflipflop;

architecture bhv of dflipflop is
begin
    process (clk, clr, set)
    begin
        -- Asynchronous clear has the highest priority
        if clr = '1' then
            q <= '0';
        -- Asynchronous set has the second-highest priority
        elsif set = '1' then
            q <= '1';
        -- Synchronous clock-based behavior
        elsif (clk'event and clk = '1') then
            q <= d;
        end if;
    end process;
end bhv;
