// Logisim project jkflipflop1.circ as structural Verilog
module main (
  input  K1,
  input  J1,
  input  CLK1,
  output Q1,
  output QN1
);

  wire nand_1_out, nand_2_out, nand_3_out, nand_4_out, nand_5_out, nand_6_out, nand_7_out, nand_8_out,
       nand_9_out, nand_10_out, not_1_out, not_2_out, not_3_out, not_4_out;

  not nand_1 (nand_1_out, K1);  // NAND_Gate
  nand nand_2 (nand_2_out, Q1, nand_1_out);
  nand nand_3 (nand_3_out, QN1, J1);
  nand nand_4 (nand_4_out, nand_2_out, nand_3_out);
  not not_1 (not_1_out, nand_4_out);
  not not_2 (not_2_out, CLK1);
  nand nand_5 (nand_5_out, nand_4_out, not_2_out);
  nand nand_6 (nand_6_out, not_2_out, not_1_out);
  nand nand_7 (nand_7_out, nand_5_out, nand_8_out);
  nand nand_8 (nand_8_out, nand_7_out, nand_6_out);
  not not_3 (not_3_out, not_2_out);
  not not_4 (not_4_out, nand_7_out);
  nand nand_9 (nand_9_out, nand_7_out, not_3_out);
  nand nand_10 (nand_10_out, not_3_out, not_4_out);
  nand nand_11 (Q1, nand_9_out, QN1);
  nand nand_12 (QN1, Q1, nand_10_out);

  // Notes on the sheet:
  //   JK flip flop
endmodule

// VHDL entity jkff, as the project stores it:
library ieee;
use ieee.std_logic_1164.all;

entity jkff is
    port (
        clk : in  std_logic;
        j   : in  std_logic;
        k   : in  std_logic;
        q   : out std_logic;
        qn  : out std_logic
    );
end entity jkff;

architecture behavioral of jkff is
    signal q_i : std_logic := '0';
begin
    process (clk)
    begin
        if rising_edge(clk) then
            if j = '0' and k = '0' then
                q_i <= q_i;        -- Hold
            elsif j = '0' and k = '1' then
                q_i <= '0';        -- Reset
            elsif j = '1' and k = '0' then
                q_i <= '1';        -- Set
            else
                q_i <= not q_i;    -- Toggle
            end if;
        end if;
    end process;

    q  <= q_i;
    qn <= not q_i;
end architecture behavioral;
