// Logisim project jkflipflop2.circ as structural Verilog
module main (
  input  clk,
  input  j,
  input  k,
  output q,
  output qn
);

  jkff jkff_1 (.clk(clk), .j(j), .k(k), .q(q), .qn(qn));
endmodule

// VHDL entity jkff, as the project stores it:
library ieee;
use ieee.std_logic_1164.all;

entity jkff is
    port (
        clk : in  std_logic;
        j   : in  std_logic;
        k   : in  std_logic;
        q   : out std_logic;
        qn  : out std_logic
    );
end entity jkff;

architecture behavioral of jkff is
    signal q_i : std_logic := '0';
begin
    process (clk)
    begin
        if rising_edge(clk) then
            if j = '0' and k = '0' then
                q_i <= q_i;        -- Hold
            elsif j = '0' and k = '1' then
                q_i <= '0';        -- Reset
            elsif j = '1' and k = '0' then
                q_i <= '1';        -- Set
            else
                q_i <= not q_i;    -- Toggle
            end if;
        end if;
    end process;

    q  <= q_i;
    qn <= not q_i;
end architecture behavioral;
