// Logisim project rslatch2.circ as structural Verilog: 1 circuit, main circuit main
module main (
  input  R1,
  input  S1,
  output Q1,
  output QN1
);

  nor nor_1 (Q1, R1, QN1);
  nor nor_2 (QN1, Q1, S1);

  // Notes on the sheet:
  //   RS Latch
endmodule
